// Logisim project UNRN-ED-Taller1.circ as structural Verilog: 7 circuits, main circuit SumCompleto_1bit
module SumCompleto_4bits (
  input  [3:0] A,
  input  [3:0] B,
  input  Cin,
  output [3:0] S,
  output Cout
);

  Hex_Digit_Display hex_digit_display_1 (.value(S));  // open: dp

  // Notes on the sheet:
  //   Sumador completo de 4 Bits
  //   Nro de Grupo: <completar>
endmodule

module SumCompleto_1bit (
  input  A,
  input  B,
  input  Cin,
  output S,
  output Cout
);

  wire and_1_out, and_2_out, xor_1_out;

  xor xor_1 (xor_1_out, A, B);
  and and_1 (and_1_out, xor_1_out, Cin);
  and and_2 (and_2_out, A, B);
  xor xor_2 (S, xor_1_out, Cin);
  or or_1 (Cout, and_1_out, and_2_out);

  // Notes on the sheet:
  //   Sumador completo de 1 Bit
  //   Nro de Grupo: 8
endmodule

module Flag_Cero (
  input  [3:0] S,
  output Z
);


  // Notes on the sheet:
  //   Flag - Cero (Z)
  //   Nro de Grupo: <completar>
endmodule

module Flag_Overflow (
  input  a3,
  input  b3,
  input  s3,
  output V
);


  // Notes on the sheet:
  //   Flag - Overflow (V)
  //   Nro de Grupo: <completar>
endmodule

module ComplementadorA2 (
  input  [3:0] B,
  input  Neg,
  output [3:0] B_star
);

  Hex_Digit_Display hex_digit_display_1 (.value(B_star));  // open: dp

  // Notes on the sheet:
  //   Complementador a 2
  //   Nro de Grupo: <completar>
  //   Neg  ALU
  //   0    B
  //   1   -B
endmodule

module UnidadAritmetica (
  input  [3:0] A,
  input  [3:0] B,
  input  OP,
  output V,
  output N,
  output Z,
  output C,
  output [3:0] S
);

  Hex_Digit_Display hex_digit_display_1 (.value(S));  // open: dp

  // Notes on the sheet:
  //   Unidad Aritmetica (Suma/Resta)
  //   Nro de Grupo: <completar>
  //   OP   ALU
  //   0  A + B
  //   1  A - B
endmodule

module ALU (
  input  [3:0] A,
  input  [3:0] B,
  input  [1:0] OP,
  output V,
  output N,
  output Z,
  output C,
  output [3:0] S
);


  // Notes on the sheet:
  //   ALU (Suma/Resta/AND/OR)
  //   Nro de Grupo: <completar>
  //   OP   ALU
  //   0 0  A + B
  //   0 1  A - B
  //   1 0  A and B
  //   1 1  A or  B
endmodule
